// Digital circuit ALU.dig as structural Verilog
module ALU (
  input  [31:0] A,
  input  [31:0] B,
  input  [6:0] ALUOp,
  output zero,
  output [31:0] alu_out
);

  wire alucontrol_1_p2, alucontrol_1_p3, not_1_out;
  wire [2:0] alucontrol_1_p4;
  wire [31:0] and_1_out, leftshifter_1_data_out, multiplexer_1_out, multiplexer_2_out, or_1_out,
       rightshifter_1_data_out, somadorvetorial_vhdl_1_p5, xor_1_out;

  // ALUControl alucontrol_1: pin names not known; wires that end beside it: ALUOp, alucontrol_1_p2, alucontrol_1_p3, alucontrol_1_p4
  // SomadorVetorial_VHDL somadorvetorial_vhdl_1: pin names not known; wires that end beside it: A, B, alucontrol_1_p3, alucontrol_1_p2, somadorvetorial_vhdl_1_p5
  EqualityComparator equalitycomparator_1 (.A(A), .B(B), .out(zero));
  RightShifter rightshifter_1 (.data_in(A), .shift_in(B[4:0]), .data_out(rightshifter_1_data_out));
  LeftShifter leftshifter_1 (.data_in(A), .shift_in(B[4:0]), .data_out(leftshifter_1_data_out));
  assign and_1_out = A & B;  // And and_1, 32 bits wide
  assign or_1_out = A | B;  // Or or_1, 32 bits wide
  assign xor_1_out = A ^ B;  // XOr xor_1, 32 bits wide
  not not_1 (not_1_out, zero);
  Multiplexer #(.Bits(32)) multiplexer_1 (.sel(zero), .in_0({32{1'b0}}), .in_1(32'h1), .out(multiplexer_1_out));
  Multiplexer #(.Bits(32)) multiplexer_2 (.sel(not_1_out), .in_0({32{1'b0}}), .in_1(32'h1), .out(multiplexer_2_out));
  Multiplexer #(.Selector_Bits(3), .Bits(32)) multiplexer_3 (
    .sel(alucontrol_1_p4), .in_0(somadorvetorial_vhdl_1_p5), .in_1(rightshifter_1_data_out),
    .in_2(multiplexer_1_out), .in_3(multiplexer_2_out), .in_4(leftshifter_1_data_out), .in_5(and_1_out),
    .in_6(or_1_out), .in_7(xor_1_out), .out(alu_out));
endmodule
