// Digital circuit AddSum.dig as structural Verilog
module AddSum (
  input  [31:0] data1,
  input  [31:0] data2,
  output [31:0] Result
);

  add_sum #(.applicationType("GHDL")) u_add_sum (.Data1(data1), .Data2(data2), .Result(Result));
endmodule

/* Code of add_sum:
library IEEE;
use IEEE.STD_LOGIC_1164.ALL;
use IEEE.NUMERIC_STD.ALL;

entity add_sum is
    Port (
        Data1  : in  STD_LOGIC_VECTOR(31 downto 0);
        Data2  : in  STD_LOGIC_VECTOR(31 downto 0);
        Result : out STD_LOGIC_VECTOR(31 downto 0)
    );
end add_sum;

architecture Behavioral of add_sum is
begin
    process(Data1, Data2)
    begin
        Result <= std_logic_vector(signed(Data1) + signed(Data2));
    end process;
end Behavioral;
*/
