// Digital circuit ControlUnitFSM.dig as structural Verilog
module ControlUnitFSM (
  output RegWrite,
  output [1:0] ALUop,
  output memRead,
  output memWRITE,
  output branch,
  output ALUSRC
);

  wire register_1_q;
  wire [7:7] undriven;

  Register register_1 (.Q(register_1_q));  // open: D, C, en
  ROM #(.AddrBits(3)) rom_1 (.sel(register_1_q), .D(RegWrite));  // open: A
  // Pins of 1 and 8 bits meet at {undriven[7], ALUop, branch, memWRITE, memRead, ALUSRC, RegWrite}
  // Pins of 1 and 2 bits meet at ALUop
endmodule
