// Digital circuit EqualityComparator.dig as structural Verilog
module EqualityComparator (
  input  [31:0] A,
  input  [31:0] B,
  output out_2
);

  EqualityComparator #(.applicationType("GHDL")) u_EqualityComparator (.A(A), .B(B), .EQ(out_2));
endmodule

/* Code of EqualityComparator:
library IEEE;
use IEEE.STD_LOGIC_1164.ALL;

entity EqualityComparator is
    port (
        A : in  STD_LOGIC_VECTOR(31 downto 0);
        B : in  STD_LOGIC_VECTOR(31 downto 0);
        EQ       : out STD_LOGIC
    );
end entity EqualityComparator;

architecture Behavioral of EqualityComparator is
begin
    EQ <= '1' when A = B else '0';

end architecture Behavioral;
*/
