// Digital circuit Estágio_Ex-Mem.dig as structural Verilog
module \Estágio_Ex_Mem  (
  input  clock,
  input  reset,
  input  turn_off,
  input  reg_write_in,
  input  mem_to_reg_in,
  input  [31:0] mem_data_in,
  input  [31:0] ALU_res_in,
  input  [4:0] rd_in,
  input  [31:0] pc_mais_4_in,
  input  [31:0] imm_in,
  output reg_write_out,
  output mem_to_reg_ou,
  output [31:0] mem_data_out,
  output [31:0] ALU_res_out,
  output [4:0] rd_out,
  output [31:0] pc_mais_4_out,
  output [31:0] imm_out
);

  ex_mem #(.applicationType("GHDL")) u_ex_mem (
    .clock(clock), .reset(reset), .turn_off(turn_off), .reg_write_in(reg_write_in),
    .mem_to_reg_in(mem_to_reg_in), .mem_data_in(mem_data_in), .ALU_res_in(ALU_res_in), .rd_in(rd_in),
    .pc_mais_4_in(pc_mais_4_in), .imm_in(imm_in), .reg_write_out(reg_write_out),
    .mem_to_reg_out(mem_to_reg_ou), .mem_data_out(mem_data_out), .ALU_res_out(ALU_res_out), .rd_out(rd_out),
    .pc_mais_4_out(pc_mais_4_out), .imm_out(imm_out));
endmodule

/* Code of ex_mem:
library IEEE;
use IEEE.STD_LOGIC_1164.ALL;
use IEEE.NUMERIC_STD.ALL;

entity ex_mem is
    Port (
        clock          : in  STD_LOGIC;
        reset          : in  STD_LOGIC;
        turn_off       : in  STD_LOGIC;

        reg_write_in   : in  STD_LOGIC;
        mem_to_reg_in  : in  STD_LOGIC;
        mem_data_in    : in  STD_LOGIC_VECTOR(31 downto 0);
        ALU_res_in     : in  STD_LOGIC_VECTOR(31 downto 0);
        rd_in          : in  STD_LOGIC_VECTOR(4 downto 0);
        pc_mais_4_in   : in  STD_LOGIC_VECTOR(31 downto 0);
        imm_in         : in  STD_LOGIC_VECTOR(31 downto 0);

        reg_write_out  : out STD_LOGIC;
        mem_to_reg_out : out STD_LOGIC;
        mem_data_out   : out STD_LOGIC_VECTOR(31 downto 0);
        ALU_res_out    : out STD_LOGIC_VECTOR(31 downto 0);
        rd_out         : out STD_LOGIC_VECTOR(4 downto 0);
        pc_mais_4_out  : out STD_LOGIC_VECTOR(31 downto 0);
        imm_out        : out STD_LOGIC_VECTOR(31 downto 0)
    );
end ex_mem;

architecture Behavioral of ex_mem is
begin
    process(clock)
    begin
        if rising_edge(clock) then
            if reset = '1' then
                reg_write_out  <= '0';
                mem_to_reg_out <= '0';
                mem_data_out   <= (others => '0');
                ALU_res_out    <= (others => '0');
                rd_out         <= (others => '0');
                pc_mais_4_out  <= (others => '0');
                imm_out        <= (others => '0');

            elsif turn_off = '0' then
                reg_write_out  <= reg_write_in;
                mem_to_reg_out <= mem_to_reg_in;
                mem_data_out   <= mem_data_in;
                ALU_res_out    <= ALU_res_in;
                rd_out         <= rd_in;
                pc_mais_4_out  <= pc_mais_4_in;
                imm_out        <= imm_in;
            end if;
        end if;
    end process;
end Behavioral;
*/
