// Digital circuit Estágio_If-Id.dig as structural Verilog
module \Estágio_If_Id  (
  input  clock,
  input  turn_off,
  input  stall,
  input  [31:0] instruction_in,
  input  [31:0] pc_in,
  output [31:0] intruction_out,
  output [31:0] pc_out,
  output [31:0] pc__plus_4_out,
  output [4:0] rs2,
  output [4:0] rs1,
  output [4:0] rd,
  output [4:0] rs2_2,
  output [4:0] rs1_2
);

  wire nor_1_out, not_1_out;
  wire [31:0] register_2_q, register_3_q, somadorvetorial_1_sum;

  SomadorVetorial somadorvetorial_1 (.A(pc_in), .B(32'h4), .vecSize(2'b11), .mode(1'b0), .sum(somadorvetorial_1_sum));
  nor nor_1 (nor_1_out, stall, turn_off);
  Register #(.Bits(32)) register_1 (.D(instruction_in), .C(clock), .en(nor_1_out), .Q(intruction_out));
  Register #(.Bits(32)) register_2 (.D(pc_in), .C(clock), .en(nor_1_out), .Q(register_2_q));
  Register #(.Bits(32)) register_3 (.D(somadorvetorial_1_sum), .C(clock), .en(nor_1_out), .Q(register_3_q));
  not not_1 (not_1_out, clock);
  Register #(.Bits(32)) register_4 (.D(register_2_q), .C(not_1_out), .en(nor_1_out), .Q(pc_out));
  Register #(.Bits(32)) register_5 (.D(register_3_q), .C(not_1_out), .en(nor_1_out), .Q(pc__plus_4_out));

  assign rd = intruction_out[11:7];
  assign rs1 = intruction_out[24:20];
  assign rs1_2 = intruction_out[24:20];
  assign rs2 = intruction_out[19:15];
  assign rs2_2 = intruction_out[19:15];

  // Notes on the sheet:
  //   pc+4
endmodule
