// Digital circuit Id-Ex.dig as structural Verilog
module Id_Ex (
);

  ID_EX_Register #(.applicationType("GHDL")) u_ID_EX_Register ();  // open: clk_i, turn_off_i, Mem_to_Reg_in, Reg_Write_in, Mem_Write_in, Mem_Read_in, ALUsrc_in, branch_in, ALUOP_in, rs1_in, rs2_in, imm_gen_in, pc_mais_4_in, rd_in, Mem_to_Reg_out, Reg_Write_out, Mem_Write_out, Mem_Read_out, ALUsrc_out, branch_out, ALUOP_out, rs1_out, rs2_out, imm_gen_out, pc_mais_4_out, rd_out
endmodule

/* Code of ID_EX_Register:
library IEEE;
use IEEE.STD_LOGIC_1164.ALL;
use IEEE.NUMERIC_STD.ALL;

entity ID_EX_Register is
    Port ( 
        clk_i           : in  STD_LOGIC;
        turn_off_i      : in  STD_LOGIC;
        Mem_to_Reg_in   : in  STD_LOGIC;
        Reg_Write_in    : in  STD_LOGIC;
        Mem_Write_in    : in  STD_LOGIC;
        Mem_Read_in     : in  STD_LOGIC;
        ALUsrc_in       : in  STD_LOGIC;
        branch_in       : in  STD_LOGIC;
        ALUOP_in        : in  STD_LOGIC_VECTOR(2 downto 0);
        rs1_in          : in  STD_LOGIC_VECTOR(31 downto 0);
        rs2_in          : in  STD_LOGIC_VECTOR(31 downto 0);
        imm_gen_in      : in  STD_LOGIC_VECTOR(31 downto 0);
        pc_mais_4_in    : in  STD_LOGIC_VECTOR(31 downto 0);
        rd_in           : in  STD_LOGIC_VECTOR(4 downto 0);
        Mem_to_Reg_out  : out STD_LOGIC;
        Reg_Write_out   : out STD_LOGIC;
        Mem_Write_out   : out STD_LOGIC;
        Mem_Read_out    : out STD_LOGIC;
        ALUsrc_out      : out STD_LOGIC;
        branch_out      : out STD_LOGIC;
        ALUOP_out       : out STD_LOGIC_VECTOR(2 downto 0);
        rs1_out         : out STD_LOGIC_VECTOR(31 downto 0);
        rs2_out         : out STD_LOGIC_VECTOR(31 downto 0);
        imm_gen_out     : out STD_LOGIC_VECTOR(31 downto 0);
        pc_mais_4_out   : out STD_LOGIC_VECTOR(31 downto 0);
        rd_out          : out STD_LOGIC_VECTOR(4 downto 0)
    );
end ID_EX_Register;

architecture Behavioral of ID_EX_Register is
begin
    process(clk_i)
    begin
        if rising_edge(clk_i) then
            if turn_off_i = '0' then
                Mem_to_Reg_out  <= Mem_to_Reg_in;
                Reg_Write_out   <= Reg_Write_in;
                Mem_Write_out   <= Mem_Write_in;
                Mem_Read_out    <= Mem_Read_in;
                ALUsrc_out      <= ALUsrc_in;
                branch_out      <= branch_in;
                ALUOP_out       <= ALUOP_in;
                rs1_out         <= rs1_in;
                rs2_out         <= rs2_in;
                imm_gen_out     <= imm_gen_in;
                pc_mais_4_out   <= pc_mais_4_in;
                rd_out          <= rd_in;
            end if;
        end if;
    end process;
end Behavioral;
*/
