// Digital circuit ImmGen.dig as structural Verilog
module ImmGen (
  input  [31:0] instruction
);

  wire instructioncomparator_1_output_1, instructioncomparator_2_output_1, instructioncomparator_3_output_1,
       instructioncomparator_4_output_1, instructioncomparator_5_output_1, instructioncomparator_6_output_1,
       instructioncomparator_7_output_1, instructioncomparator_8_output_1, or_1_out, or_2_out;
  wire [2:0] priorityencoder_1_num;

  // NotConnected on instruction[7]
  InstructionComparator instructioncomparator_1 (
    .opcode(instruction[6:0]), .constante(7'b0000011), .output_1(instructioncomparator_1_output_1));
  InstructionComparator instructioncomparator_2 (
    .opcode(instruction[6:0]), .constante(7'b0010011), .output_1(instructioncomparator_2_output_1));
  InstructionComparator instructioncomparator_3 (
    .opcode(instruction[6:0]), .constante(7'b1100111), .output_1(instructioncomparator_3_output_1));
  InstructionComparator instructioncomparator_4 (
    .opcode(instruction[6:0]), .constante(7'b0100011), .output_1(instructioncomparator_4_output_1));
  InstructionComparator instructioncomparator_5 (
    .opcode(instruction[6:0]), .constante(7'b1100011), .output_1(instructioncomparator_5_output_1));
  InstructionComparator instructioncomparator_6 (
    .opcode(instruction[6:0]), .constante(7'b0110111), .output_1(instructioncomparator_6_output_1));
  InstructionComparator instructioncomparator_7 (
    .opcode(instruction[6:0]), .constante(7'b0010111), .output_1(instructioncomparator_7_output_1));
  InstructionComparator instructioncomparator_8 (
    .opcode(instruction[6:0]), .constante(7'b1101111), .output_1(instructioncomparator_8_output_1));
  or or_1 (or_1_out, instructioncomparator_1_output_1, instructioncomparator_2_output_1, instructioncomparator_3_output_1);
  or or_2 (or_2_out, instructioncomparator_6_output_1, instructioncomparator_7_output_1);
  PriorityEncoder #(.Selector_Bits(3)) priorityencoder_1 (
    .in0(or_1_out), .in1(instructioncomparator_4_output_1), .in2(instructioncomparator_5_output_1),
    .in3(or_2_out), .in4(instructioncomparator_8_output_1), .in5(1'b0), .in6(1'b0), .in7(1'b0),
    .num(priorityencoder_1_num));  // open: any
  // Pins of 1 and 25 bits meet at instruction[31:7]

  // Notes on the sheet:
  //   I
  //   S
  //   SB
  //   UJ
  //   U
endmodule
