// Digital circuit InstructionComparator.dig as structural Verilog
module InstructionComparator (
  input  [6:0] opcode,
  input  [6:0] constante,
  output output_1
);

  instruct_comparator #(.applicationType("GHDL")) u_instruct_comparator (
    .opcode(opcode), .constante(constante), .output_1(output_1));
endmodule

/* Code of instruct_comparator:
library IEEE;
use IEEE.STD_LOGIC_1164.ALL;

entity instruct_comparator is
    port (
        opcode    : in  STD_LOGIC_VECTOR(6 downto 0);
        constante : in  STD_LOGIC_VECTOR(6 downto 0);
        output_1  : out STD_LOGIC
    );
end entity instruct_comparator;

architecture Behavioral of instruct_comparator is
begin
    output_1 <= '1' when (opcode = constante) else '0';
end architecture Behavioral;
*/
