// Digital circuit InstructionDecoder.dig as structural Verilog
module InstructionDecoder (
  input  [31:0] instruction,
  output [6:0] opcode,
  output [4:0] rd,
  output [4:0] funct3,
  output [4:0] rs1,
  output [6:0] funct7,
  output [4:0] rs2
);

  // Pins of 8 and 32 bits meet at instruction
  // Pins of 3 and 5 bits meet at funct3
  // Pins of 3 and 5 bits meet at rs1
  // Pins of 3 and 7 bits meet at instruction[6:0]

  assign funct7 = instruction[6:0];
  assign rs2[0] = instruction[7];
endmodule
