// Digital circuit InstructionRom.dig as structural Verilog
module InstructionRom (
  input  [7:0] in,
  output [31:0] out
);

  Instruction_ROM #(.applicationType("GHDL")) u_Instruction_ROM (.address_i(in), .instruction_o(out));
endmodule

/* Code of Instruction_ROM:
library IEEE;
use IEEE.STD_LOGIC_1164.ALL;
use IEEE.NUMERIC_STD.ALL;

-- Componente: Instruction_ROM
-- Descrição: Memória de Apenas Leitura (ROM) para armazenar as instruções do programa.
--            É endereçada pelo Program Counter (PC) e retorna a instrução de 32 bits.
entity Instruction_ROM is
    Port ( 
        address_i     : in  STD_LOGIC_VECTOR (7 downto 0);
        instruction_o : out STD_LOGIC_VECTOR (31 downto 0)
    );
end Instruction_ROM;

architecture Behavioral of Instruction_ROM is
    
    type rom_type is array (0 to 255) of STD_LOGIC_VECTOR (31 downto 0);

    constant ROM : rom_type := (
        x"00500093",  -- 0: addi x1, x0, 5
        x"00A00113",  -- 1: addi x2, x0, 10
        x"002081B3",  -- 2: add  x3, x1, x2
        x"02302623",  -- 3: sw   x3, 12(x0)
        others       => x"00000000"
    );

begin

    instruction_o <= ROM(to_integer(unsigned(address_i)));

end Behavioral;
*/
