// Digital circuit LeftShifter.dig as structural Verilog
module LeftShifter (
  input  [31:0] data_in,
  input  [4:0] shift_in,
  output [31:0] data_out
);

  LeftShifter #(.applicationType("GHDL")) u_LeftShifter (
    .data_in_i(data_in), .shift_amount_i(shift_in), .data_out_o(data_out));
endmodule

/* Code of LeftShifter:
library IEEE;
use IEEE.STD_LOGIC_1164.ALL;
use IEEE.NUMERIC_STD.ALL;

-- Componente: LeftShifter
-- Descrição: Deslocador lógico para a esquerda.
entity LeftShifter is
    Port ( 
        data_in_i      : in  STD_LOGIC_VECTOR (31 downto 0);
        shift_amount_i : in  STD_LOGIC_VECTOR (4 downto 0); -- 5 bits para deslocar até 31 posições
        data_out_o     : out STD_LOGIC_VECTOR (31 downto 0)
    );
end LeftShifter;

architecture Behavioral of LeftShifter is
begin
    data_out_o <= std_logic_vector(shift_left(unsigned(data_in_i), to_integer(unsigned(shift_amount_i))));
end Behavioral;
*/
