// Digital circuit cpu.dig as structural Verilog
module cpu (
  input  stall,
  input  [31:0] instruction_in,
  input  [31:0] pc_in,
  input  reset,
  input  clock,
  input  turn_off
);

  wire alu_1_zero, control_1_alusrc1, control_1_branch, control_1_memread, control_1_memtoreg,
       control_1_memwrite, control_1_regwrite, \estágio_ex_mem_1_p16 , \estágio_ex_mem_1_p18 ,
       \estágio_ex_mem_1_p19 , \estágio_id_ex_1_p12 , \estágio_id_ex_1_p15 , \estágio_id_ex_1_p16 ,
       \estágio_id_ex_1_p17 , \estágio_id_ex_1_p18 , \estágio_id_ex_1_p19 , \estágio_id_ex_1_p20 ,
       \estágio_id_ex_1_p26 , \estágio_mem_wb_1_p12 , forward_unit_1_p2, forward_unit_1_p3, hazardunit_1_p6;
  wire [1:0] control_1_aluop, forward_unit_1_p8, forward_unit_1_p9;
  wire [2:0] \estágio_id_ex_1_p21 ;
  wire [4:0] \estágio_if_id_1_rd , \estágio_if_id_1_rs1 , \estágio_if_id_1_rs1_2 , \estágio_if_id_1_rs2 ,
       \estágio_if_id_1_rs2_2 , forward_unit_1_p7;
  wire [31:0] addsum_1_result, alu_1_alu_out, \estágio_id_ex_1_p22 , \estágio_id_ex_1_p23 ,
       \estágio_id_ex_1_p24 , \estágio_id_ex_1_p25 , \estágio_if_id_1_intruction_out ,
       \estágio_if_id_1_pc__plus_4_out , \estágio_mem_wb_1_p13 , \estágio_mem_wb_1_p14 , multiplexer_1_out,
       multiplexer_2_out, multiplexer_3_out, multiplexer_4_out, registers_1_read_data1,
       registers_1_read_data2, write_data;

  \Estágio_If_Id  \estágio_if_id_1  (
    .clock(clock), .turn_off(turn_off), .stall(hazardunit_1_p6), .instruction_in(instruction_in),
    .pc_in(pc_in), .reset(reset), .intruction_out(\estágio_if_id_1_intruction_out ),
    .pc__plus_4_out(\estágio_if_id_1_pc__plus_4_out ), .rs2(\estágio_if_id_1_rs2 ),
    .rs1(\estágio_if_id_1_rs1 ), .rd(\estágio_if_id_1_rd ), .rs2_2(\estágio_if_id_1_rs2_2 ),
    .rs1_2(\estágio_if_id_1_rs1_2 ));  // open: pc_out
  ImmGen immgen_1 (.instruction(\estágio_if_id_1_intruction_out ));
  Control control_1 (
    .instruction(\estágio_if_id_1_intruction_out ), .clock(clock), .reset(reset),
    .ALUsrc1(control_1_alusrc1), .ALUOp(control_1_aluop), .ALUsrc(control_1_alusrc1),
    .branch(control_1_branch), .MemRead(control_1_memread), .MemWrite(control_1_memwrite),
    .RegWrite(control_1_regwrite), .MemToReg(control_1_memtoreg));  // open: jump
  Registers registers_1 (
    .read_register_2(\estágio_if_id_1_rs1 ), .write_register(forward_unit_1_p7),
    .read_register_1(\estágio_if_id_1_rs2 ), .write_data(write_data), .clock(clock),
    .write(forward_unit_1_p2), .read_data1(registers_1_read_data1), .read_data2(registers_1_read_data2));
  // Estágio_Id_Ex estágio_id_ex_1: pin names not known; wires that end beside it: clock, turn_off, control_1_memtoreg, control_1_regwrite, control_1_memwrite, control_1_memread, control_1_alusrc1, control_1_branch, control_1_aluop, registers_1_read_data1, registers_1_read_data2, \estágio_id_ex_1_p12 , \estágio_if_id_1_pc__plus_4_out , \estágio_if_id_1_rd , \estágio_id_ex_1_p15 , \estágio_id_ex_1_p16 , \estágio_id_ex_1_p17 , \estágio_id_ex_1_p18 , \estágio_id_ex_1_p19 , \estágio_id_ex_1_p20 , \estágio_id_ex_1_p21 , \estágio_id_ex_1_p22 , \estágio_id_ex_1_p23 , \estágio_id_ex_1_p24 , \estágio_id_ex_1_p25 , \estágio_id_ex_1_p26 
  // HazardUnit hazardunit_1: pin names not known; wires that end beside it: clock, \estágio_if_id_1_rs1_2 , \estágio_if_id_1_rs2_2 , \estágio_id_ex_1_p26 , \estágio_id_ex_1_p18 , hazardunit_1_p6
  // Forward_Unit forward_unit_1: pin names not known; wires that end beside it: clock, forward_unit_1_p2, forward_unit_1_p3, \estágio_id_ex_1_p22 [4:0], \estágio_id_ex_1_p23 [4:0], \estágio_id_ex_1_p26 , forward_unit_1_p7, forward_unit_1_p8, forward_unit_1_p9
  Multiplexer #(.Bits(32)) multiplexer_1 (
    .sel(\estágio_id_ex_1_p19 ), .in_0(\estágio_id_ex_1_p24 ), .in_1(\estágio_id_ex_1_p25 ),
    .out(multiplexer_1_out));
  Multiplexer #(.Bits(32)) multiplexer_2 (
    .sel(\estágio_id_ex_1_p19 ), .in_0(\estágio_id_ex_1_p23 ), .in_1(\estágio_id_ex_1_p24 ),
    .out(multiplexer_2_out));
  AddSum addsum_1 (.data1(\estágio_id_ex_1_p25 ), .data2(\estágio_id_ex_1_p24 ), .Result(addsum_1_result));
  Multiplexer #(.Bits(32), .Selector_Bits(2)) multiplexer_3 (
    .sel(forward_unit_1_p8), .in_0({32{1'b0}}), .in_1({32{1'b0}}), .in_2(multiplexer_1_out),
    .in_3({32{1'b0}}), .out(multiplexer_3_out));
  Multiplexer #(.Bits(32), .Selector_Bits(2)) multiplexer_4 (
    .sel(forward_unit_1_p9), .in_0({32{1'b0}}), .in_1(multiplexer_2_out), .in_2({32{1'b0}}),
    .in_3({32{1'b0}}), .out(multiplexer_4_out));
  ALU alu_1 (
    .A(multiplexer_3_out), .B(multiplexer_4_out), .ALUOp({4'b0000, \estágio_id_ex_1_p21 }),
    .zero(alu_1_zero), .alu_out(alu_1_alu_out));
  // Estágio_Ex_Mem estágio_ex_mem_1: pin names not known; wires that end beside it: clock, reset, alu_1_zero, \estágio_id_ex_1_p20 , \estágio_id_ex_1_p18 , \estágio_id_ex_1_p17 , \estágio_id_ex_1_p16 , \estágio_id_ex_1_p15 , \estágio_id_ex_1_p19 , \estágio_id_ex_1_p23 , alu_1_alu_out, \estágio_id_ex_1_p25 , addsum_1_result, \estágio_id_ex_1_p24 , \estágio_id_ex_1_p26 , \estágio_ex_mem_1_p16 , forward_unit_1_p3, \estágio_ex_mem_1_p18 , \estágio_ex_mem_1_p19 
  // Estágio_Mem_Wb estágio_mem_wb_1: pin names not known; wires that end beside it: clock, reset, turn_off, \estágio_ex_mem_1_p16 , forward_unit_1_p3, \estágio_ex_mem_1_p18 , alu_1_alu_out, \estágio_id_ex_1_p26 , \estágio_ex_mem_1_p19 , addsum_1_result, forward_unit_1_p2, \estágio_mem_wb_1_p12 , \estágio_mem_wb_1_p13 , \estágio_mem_wb_1_p14 , forward_unit_1_p7
  Multiplexer #(.Bits(32)) multiplexer_5 (
    .sel(\estágio_mem_wb_1_p12 ), .in_0(\estágio_mem_wb_1_p13 ), .in_1(\estágio_mem_wb_1_p14 ),
    .out(write_data));
endmodule
