// Digital circuit RightShifter.dig as structural Verilog
module RightShifter (
  input  [31:0] data_in,
  input  [4:0] shift_in,
  output [31:0] data_out
);

  RightShifter #(.applicationType("GHDL")) u_RightShifter (
    .data_in_i(data_in), .shift_amount_i(shift_in), .data_out_o(data_out));
endmodule

/* Code of RightShifter:
library IEEE;
use IEEE.STD_LOGIC_1164.ALL;
use IEEE.NUMERIC_STD.ALL;

-- Componente: RightShifter
-- Descrição: Deslocador lógico para a direita.
entity RightShifter is
    Port ( 
        data_in_i      : in  STD_LOGIC_VECTOR (31 downto 0);
        shift_amount_i : in  STD_LOGIC_VECTOR (4 downto 0);
        data_out_o     : out STD_LOGIC_VECTOR (31 downto 0)
    );
end RightShifter;

architecture Behavioral of RightShifter is
begin
    data_out_o <= std_logic_vector(shift_right(unsigned(data_in_i), to_integer(unsigned(shift_amount_i))));
end Behavioral;
*/
