// Digital circuit SomadorVetorial.dig as structural Verilog
module SomadorVetorial (
  input  mode_i,
  input  [1:0] vecSize,
  input  [7:0] Adress,
  input  [31:0] DataIn,
  input  Store,
  input  Async,
  input  Clock,
  input  Load,
  input  [4:0] in_10,
  input  [4:0] in_11,
  input  [4:0] in_12,
  input  [31:0] DataIn_2,
  input  in_14,
  output lookAhead_out,
  output [31:0] sum_out
);

  wire and_2_out, and_3_out, dip_out, not_1_out, or_1_out, u_LookAhead4Bit_2_cout, u_LookAhead4Bit_3_cout,
       u_LookAhead4Bit_4_cout, u_LookAhead4Bit_5_cout, u_LookAhead4Bit_6_cout, u_LookAhead4Bit_7_cout,
       u_LookAhead4Bit_cout;
  wire [3:0] u_LookAhead4Bit_2_s, u_LookAhead4Bit_3_s, u_LookAhead4Bit_4_s, u_LookAhead4Bit_5_s,
       u_LookAhead4Bit_6_s, u_LookAhead4Bit_7_s, u_LookAhead4Bit_8_s, u_LookAhead4Bit_s,
       u_propagation_generator_2_vec_g, u_propagation_generator_2_vec_p, u_propagation_generator_3_vec_g,
       u_propagation_generator_3_vec_p, u_propagation_generator_4_vec_g, u_propagation_generator_4_vec_p,
       u_propagation_generator_5_vec_g, u_propagation_generator_5_vec_p, u_propagation_generator_6_vec_g,
       u_propagation_generator_6_vec_p, u_propagation_generator_7_vec_g, u_propagation_generator_7_vec_p,
       u_propagation_generator_8_vec_g, u_propagation_generator_8_vec_p, u_propagation_generator_vec_g,
       u_propagation_generator_vec_p, u_signal_decoder_a0, u_signal_decoder_a1, u_signal_decoder_a2,
       u_signal_decoder_a3, u_signal_decoder_a4, u_signal_decoder_a5, u_signal_decoder_a6,
       u_signal_decoder_a7, u_signal_decoder_b0, u_signal_decoder_b1, u_signal_decoder_b2,
       u_signal_decoder_b3, u_signal_decoder_b4, u_signal_decoder_b5, u_signal_decoder_b6,
       u_signal_decoder_b7;
  wire [31:0] and_1_out, bancoregistradores_1_readdata1, bancoregistradores_1_readdata2, bitextender_1_out,
       bitextender_2_out, multiplexer_1_out, ram32bit_1_p7, u_inverter_s;

  BitExtender #(.inputBits(1), .outputBits(32)) bitextender_1 (.in(Store), .out(bitextender_1_out));
  not not_1 (not_1_out, Async);
  Multiplexer #(.Bits(32)) multiplexer_1 (.sel(dip_out), .in_0(DataIn_2), .in_1(sum_out), .out(multiplexer_1_out));
  assign and_1_out = DataIn & bitextender_1_out;  // And and_1, 32 bits wide
  and and_2 (and_2_out, Store, not_1_out);
  DipSwitch dip (.out(dip_out));
  and and_3 (and_3_out, Async, Store);
  or or_1 (or_1_out, and_3_out, and_2_out);
  BancoRegistradores bancoregistradores_1 (
    .rs_2(in_10), .rd(in_12), .rs_1(in_11), .WriteData(multiplexer_1_out), .Clock(Clock), .regWrite(in_14),
    .readData1(bancoregistradores_1_readdata1), .readData2(bancoregistradores_1_readdata2));
  // RAM32Bit #(.generic("addrBits :=8 ;")) ram32bit_1: pin names not known; wires that end beside it: Adress, and_1_out, or_1_out, 2'b00, 1'b0, Clock, ram32bit_1_p7
  // And and_4 has open pins: In_1=ram32bit_1_p7, In_2=bitextender_2_out, out=open
  BitExtender #(.inputBits(1), .outputBits(32)) bitextender_2 (.in(Load), .out(bitextender_2_out));
  inverter #(.applicationType("GHDL")) u_inverter (.a(bancoregistradores_1_readdata2), .sel(mode_i), .s(u_inverter_s));
  signal_decoder #(.applicationType("GHDL")) u_signal_decoder (
    .a(bancoregistradores_1_readdata1), .b(u_inverter_s), .a0(u_signal_decoder_a0), .a1(u_signal_decoder_a1),
    .a2(u_signal_decoder_a2), .a3(u_signal_decoder_a3), .a4(u_signal_decoder_a4), .a5(u_signal_decoder_a5),
    .a6(u_signal_decoder_a6), .a7(u_signal_decoder_a7), .b0(u_signal_decoder_b0), .b1(u_signal_decoder_b1),
    .b2(u_signal_decoder_b2), .b3(u_signal_decoder_b3), .b4(u_signal_decoder_b4), .b5(u_signal_decoder_b5),
    .b6(u_signal_decoder_b6), .b7(u_signal_decoder_b7));
  propagation_generator #(.applicationType("GHDL")) u_propagation_generator (
    .a(u_signal_decoder_a0), .b(u_signal_decoder_b0), .vec_p(u_propagation_generator_vec_p),
    .vec_g(u_propagation_generator_vec_g));
  propagation_generator #(.applicationType("GHDL")) u_propagation_generator_2 (
    .a(u_signal_decoder_a1), .b(u_signal_decoder_b1), .vec_p(u_propagation_generator_2_vec_p),
    .vec_g(u_propagation_generator_2_vec_g));
  propagation_generator #(.applicationType("GHDL")) u_propagation_generator_3 (
    .a(u_signal_decoder_a2), .b(u_signal_decoder_b2), .vec_p(u_propagation_generator_3_vec_p),
    .vec_g(u_propagation_generator_3_vec_g));
  propagation_generator #(.applicationType("GHDL")) u_propagation_generator_4 (
    .a(u_signal_decoder_a3), .b(u_signal_decoder_b3), .vec_p(u_propagation_generator_4_vec_p),
    .vec_g(u_propagation_generator_4_vec_g));
  propagation_generator #(.applicationType("GHDL")) u_propagation_generator_5 (
    .a(u_signal_decoder_a4), .b(u_signal_decoder_b4), .vec_p(u_propagation_generator_5_vec_p),
    .vec_g(u_propagation_generator_5_vec_g));
  propagation_generator #(.applicationType("GHDL")) u_propagation_generator_6 (
    .a(u_signal_decoder_a5), .b(u_signal_decoder_b5), .vec_p(u_propagation_generator_6_vec_p),
    .vec_g(u_propagation_generator_6_vec_g));
  propagation_generator #(.applicationType("GHDL")) u_propagation_generator_7 (
    .a(u_signal_decoder_a6), .b(u_signal_decoder_b6), .vec_p(u_propagation_generator_7_vec_p),
    .vec_g(u_propagation_generator_7_vec_g));
  propagation_generator #(.applicationType("GHDL")) u_propagation_generator_8 (
    .a(u_signal_decoder_a7), .b(u_signal_decoder_b7), .vec_p(u_propagation_generator_8_vec_p),
    .vec_g(u_propagation_generator_8_vec_g));
  LookAhead4Bit #(.applicationType("GHDL")) u_LookAhead4Bit (
    .p(u_propagation_generator_vec_p), .g(u_propagation_generator_vec_g), .cin(mode_i),
    .cout(u_LookAhead4Bit_cout), .s(u_LookAhead4Bit_s));
  LookAhead4Bit #(.applicationType("GHDL")) u_LookAhead4Bit_2 (
    .p(u_propagation_generator_2_vec_p), .g(u_propagation_generator_2_vec_g), .cin(u_LookAhead4Bit_cout),
    .cout(u_LookAhead4Bit_2_cout), .s(u_LookAhead4Bit_2_s));
  LookAhead4Bit #(.applicationType("GHDL")) u_LookAhead4Bit_3 (
    .p(u_propagation_generator_3_vec_p), .g(u_propagation_generator_3_vec_g), .cin(u_LookAhead4Bit_2_cout),
    .cout(u_LookAhead4Bit_3_cout), .s(u_LookAhead4Bit_3_s));
  LookAhead4Bit #(.applicationType("GHDL")) u_LookAhead4Bit_4 (
    .p(u_propagation_generator_4_vec_p), .g(u_propagation_generator_4_vec_g), .cin(u_LookAhead4Bit_3_cout),
    .cout(u_LookAhead4Bit_4_cout), .s(u_LookAhead4Bit_4_s));
  LookAhead4Bit #(.applicationType("GHDL")) u_LookAhead4Bit_5 (
    .p(u_propagation_generator_5_vec_p), .g(u_propagation_generator_5_vec_g), .cin(u_LookAhead4Bit_4_cout),
    .cout(u_LookAhead4Bit_5_cout), .s(u_LookAhead4Bit_5_s));
  LookAhead4Bit #(.applicationType("GHDL")) u_LookAhead4Bit_6 (
    .p(u_propagation_generator_6_vec_p), .g(u_propagation_generator_6_vec_g), .cin(u_LookAhead4Bit_5_cout),
    .cout(u_LookAhead4Bit_6_cout), .s(u_LookAhead4Bit_6_s));
  LookAhead4Bit #(.applicationType("GHDL")) u_LookAhead4Bit_7 (
    .p(u_propagation_generator_7_vec_p), .g(u_propagation_generator_7_vec_g), .cin(u_LookAhead4Bit_6_cout),
    .cout(u_LookAhead4Bit_7_cout), .s(u_LookAhead4Bit_7_s));
  LookAhead4Bit #(.applicationType("GHDL")) u_LookAhead4Bit_8 (
    .p(u_propagation_generator_8_vec_p), .g(u_propagation_generator_8_vec_g), .cin(u_LookAhead4Bit_7_cout),
    .cout(lookAhead_out), .s(u_LookAhead4Bit_8_s));
  output_size #(.applicationType("GHDL")) u_output_size (
    .s0(u_LookAhead4Bit_s), .s1(u_LookAhead4Bit_2_s), .s2(u_LookAhead4Bit_3_s), .s3(u_LookAhead4Bit_4_s),
    .s4(u_LookAhead4Bit_5_s), .s5(u_LookAhead4Bit_6_s), .s6(u_LookAhead4Bit_7_s), .s7(u_LookAhead4Bit_8_s),
    .sel(vecSize), .s(sum_out));

  // Notes on the sheet:
  //   vecSize: default 3
endmodule

/* Code of inverter:
LIBRARY ieee;
USE ieee.std_logic_1164.ALL;

ENTITY inverter IS
    PORT (
        a : IN STD_LOGIC_VECTOR(31 DOWNTO 0);
        sel : IN STD_LOGIC;
        s : OUT STD_LOGIC_VECTOR(31 DOWNTO 0)
    );
END inverter;

ARCHITECTURE behavior OF inverter IS
BEGIN
    PROCESS (a, sel)
    BEGIN
        CASE sel IS
            WHEN '1' =>
                s <= NOT a;
            WHEN '0' =>
                s <= a;
            WHEN OTHERS =>
                s <= (others => '0');
        END CASE;
    END PROCESS;
END behavior;
*/

/* Code of signal_decoder:
LIBRARY ieee;
USE ieee.std_logic_1164.ALL;

ENTITY signal_decoder IS
    PORT (
        a, b : IN STD_LOGIC_VECTOR(31 DOWNTO 0);
        a0, a1, a2, a3, a4, a5, a6, a7, b0, b1, b2, b3, b4, b5, b6, b7 : OUT STD_LOGIC_VECTOR(3 DOWNTO 0)
    );
END signal_decoder;

ARCHITECTURE Behavioral OF signal_decoder IS

BEGIN
    a0 <= a(3 DOWNTO 0);
    a1 <= a(7 DOWNTO 4);
    a2 <= a(11 DOWNTO 8);
    a3 <= a(15 DOWNTO 12);
    a4 <= a(19 DOWNTO 16);
    a5 <= a(23 DOWNTO 20);
    a6 <= a(27 DOWNTO 24);
    a7 <= a(31 DOWNTO 28);

    b0 <= b(3 DOWNTO 0);
    b1 <= b(7 DOWNTO 4);
    b2 <= b(11 DOWNTO 8);
    b3 <= b(15 DOWNTO 12);
    b4 <= b(19 DOWNTO 16);
    b5 <= b(23 DOWNTO 20);
    b6 <= b(27 DOWNTO 24);
    b7 <= b(31 DOWNTO 28);
END Behavioral;
*/

/* Code of propagation_generator:
-- propagation generator for CLA 4-Bit Adder

LIBRARY ieee;
USE ieee.std_logic_1164.ALL;

ENTITY propagation_generator IS
    PORT (
        a, b : IN STD_LOGIC_VECTOR(3 DOWNTO 0);
        vec_p, vec_g : OUT STD_LOGIC_VECTOR(3 DOWNTO 0)

    );
END propagation_generator;

ARCHITECTURE behavior OF propagation_generator IS

BEGIN
    PROCESS (a, b)
    BEGIN
	vec_p <= a xor b;
        vec_g <= a and b;


    END PROCESS;

END behavior;
*/

/* Code of LookAhead4Bit:
-- LookAhead 4-Bit

LIBRARY ieee;
use ieee.std_logic_1164.all;

ENTITY LookAhead4Bit IS
    PORT(
        p, g : IN STD_LOGIC_VECTOR(3 DOWNTO 0);
        cin : IN STD_LOGIC;
	cout : OUT STD_LOGIC;
        s : OUT STD_LOGIC_VECTOR(3 DOWNTO 0)

    );
END LookAhead4Bit;

ARCHITECTURE LookAhead4Bit OF LookAhead4Bit IS
signal c1, c2, c3, c4 : STD_LOGIC;

BEGIN
    c1 <= g(0) OR (p(0) AND cin);
    c2 <= g(1) OR (p(1) AND (g(0) OR (p(0) AND cin)));
    c3 <= g(2) OR (p(2) AND (g(1) OR (p(1) AND (g(0) OR (p(0) AND cin)))));
    c4 <= g(3) OR (p(3) AND (g(2) OR (p(2) AND (g(1) OR (p(1) AND (g(0) OR (p(0) AND cin)))))));

    s(0) <= p(0) XOR cin;
    s(1) <= p(1) XOR c1;
    s(2) <= p(2) XOR c2;
    s(3) <= p(3) XOR c3;	
    cout <= c4;
	
END LookAhead4Bit;
*/

/* Code of output_size:
-- moduling different sizes of adders

LIBRARY ieee;
use ieee.std_logic_1164.ALL;
use ieee.numeric_std.all;

ENTITY output_size IS
    PORT (
        s0, s1, s2, s3, s4, s5, s6, s7 : IN STD_LOGIC_VECTOR(3 DOWNTO 0);
        sel : IN STD_LOGIC_VECTOR(1 DOWNTO 0);
        s : OUT STD_LOGIC_VECTOR(31 DOWNTO 0)
    );
END output_size;

ARCHITECTURE behavior OF output_size IS
    SIGNAL s_int : STD_LOGIC_VECTOR(31 DOWNTO 0);

BEGIN
    s_int(3 DOWNTO 0) <= s0;
    s_int(7 DOWNTO 4) <= s1;
    s_int(11 DOWNTO 8) <= s2;
    s_int(15 DOWNTO 12) <= s3;
    s_int(19 DOWNTO 16) <= s4;
    s_int(23 DOWNTO 20) <= s5;
    s_int(27 DOWNTO 24) <= s6;
    s_int(31 DOWNTO 28) <= s7;

    PROCESS (sel)
    BEGIN
        CASE sel IS
            WHEN "00" =>
                s <= std_logic_vector(unsigned(s_int) and x"0000000F");
            WHEN "01" =>
                s <= std_logic_vector(unsigned(s_int) and x"000000FF");
            WHEN "10" =>
                s <= std_logic_vector(unsigned(s_int) and x"0000FFFF");
            WHEN "11" =>
                s <= s_int;
            WHEN OTHERS =>
                s <= "00000000000000000000000000000000";
        END CASE;
    END PROCESS;
END behavior;
*/
